# Fritzing sketch Gate Counter (saved by Fritzing 1.0.3b)

parts:
  A1 = Micro SD card reader
  A2 = ESP32 DevKitc V4
  J1 = female pin header, 5 pins [form="♀ (female)"]
  J2 = female pin header, 4 pins [form="♀ (female)"]
  J3 = female pin header, 3 pins [form="♀ (female)"]
  J4 = female pin header, 3 pins [form="♀ (female)"]
  J5 = female pin header, 2 pins [form="♀ (female)"]  # not connected
  J6 = female pin header, 2 pins [form="♀ (female)"]  # not connected

nets:
  N1: A1.Pin_1, A2.Pin_1, J1.pin1, J2.pin2, J3.pin1, J4.pin1
  N2: A1.Pin_2, A2.Pin_29
  N3: A1.Pin_3, A2.Pin_37
  N4: A1.Pin_4, A2.Pin_30
  N5: A1.Pin_5, A2.Pin_31
  N6: A1.Pin_6, A2.Pin_14, A2.Pin_32, J1.pin5, J2.pin1, J3.pin3, J4.pin3
  N7: A2.Pin_27, J4.pin2
  N8: A2.Pin_28, J3.pin2
  N9: A2.Pin_33, J1.pin2, J2.pin4
  N10: A2.Pin_36, J1.pin3, J2.pin3

notes:
  DS3231 PI RTC
  0.96 Inch OLED I2C IIC Display Module
  Gate Counter Schematic
  GAL 10/10/24
  BeamSensor 16
  MagSensor 17

custom parts:
  Micro SD card reader: Micro SD card reader.
  ESP32 DevKitc V4: ESP32-DevKitC board with ESP32-WROOM-32 module. ESP32-DevKitC V4 is a small-sized ESP32-based development board produced by Espressif. Most of the pins on the ESP module are broken out to the pin headers on the board. The pins D0, D1, D2, D3, CMD and CLK are used internally for communication between ESP32 and SPI flash memory. They are grouped on both sides near the USB connector. Avoid using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
